// Logisim project 32Adder.circ as structural Verilog: 1 circuit, main circuit main
module main (
  input  [31:0] a_i,
  input  [31:0] b_i,
  output c_out,
  output r_31,
  output r_30,
  output r_29,
  output r_28,
  output r_27,
  output r_26,
  output r_25,
  output r_24,
  output r_23,
  output r_22,
  output r_21,
  output r_20,
  output r_19,
  output r_18,
  output r_17,
  output r_16,
  output r_15,
  output r_14,
  output r_13,
  output r_12,
  output r_11,
  output r_10,
  output r_9,
  output r_8,
  output r_7,
  output r_6,
  output r_5,
  output r_4,
  output r_3,
  output r_2,
  output r_1,
  output r_0
);

  wire _1_c_i_1, _2_c_i_1, _3_c_i_1, _4_c_i_1, _5_c_i_1, _6_c_i_1, _7_c_i_1, _8_c_i_1, _9_c_i_1, _10_c_i_1,
       _11_c_i_1, _12_c_i_1, _13_c_i_1, _14_c_i_1, _15_c_i_1, _16_c_i_1, _17_c_i_1, _18_c_i_1, _19_c_i_1,
       _20_c_i_1, _21_c_i_1, _22_c_i_1, _23_c_i_1, _24_c_i_1, _25_c_i_1, _26_c_i_1, _27_c_i_1, _28_c_i_1,
       _29_c_i_1, _30_c_i_1, main_1_c_i_1;

  fullAdder_main _31 (.c_i_1(c_out), .s_i(r_31), .a_i(a_i[31]), .b_i(b_i[31]), .c_i(_30_c_i_1));
  fullAdder_main _30 (.c_i_1(_30_c_i_1), .s_i(r_30), .a_i(a_i[30]), .b_i(b_i[30]), .c_i(_29_c_i_1));
  fullAdder_main _28 (.c_i_1(_28_c_i_1), .s_i(r_28), .a_i(a_i[28]), .b_i(b_i[28]), .c_i(_27_c_i_1));
  fullAdder_main _29 (.c_i_1(_29_c_i_1), .s_i(r_29), .a_i(a_i[29]), .b_i(b_i[29]), .c_i(_28_c_i_1));
  fullAdder_main _27 (.c_i_1(_27_c_i_1), .s_i(r_27), .a_i(a_i[27]), .b_i(b_i[27]), .c_i(_26_c_i_1));
  fullAdder_main _26 (.c_i_1(_26_c_i_1), .s_i(r_26), .a_i(a_i[26]), .b_i(b_i[26]), .c_i(_25_c_i_1));
  fullAdder_main _25 (.c_i_1(_25_c_i_1), .s_i(r_25), .a_i(a_i[25]), .b_i(b_i[25]), .c_i(_24_c_i_1));
  fullAdder_main _24 (.c_i_1(_24_c_i_1), .s_i(r_24), .a_i(a_i[24]), .b_i(b_i[24]), .c_i(_23_c_i_1));
  fullAdder_main _23 (.c_i_1(_23_c_i_1), .s_i(r_23), .a_i(a_i[23]), .b_i(b_i[23]), .c_i(_22_c_i_1));
  fullAdder_main _22 (.c_i_1(_22_c_i_1), .s_i(r_22), .a_i(a_i[22]), .b_i(b_i[22]), .c_i(_21_c_i_1));
  fullAdder_main _20 (.c_i_1(_20_c_i_1), .s_i(r_20), .a_i(a_i[20]), .b_i(b_i[20]), .c_i(_19_c_i_1));
  fullAdder_main _21 (.c_i_1(_21_c_i_1), .s_i(r_21), .a_i(a_i[21]), .b_i(b_i[21]), .c_i(_20_c_i_1));
  fullAdder_main _19 (.c_i_1(_19_c_i_1), .s_i(r_19), .a_i(a_i[19]), .b_i(b_i[19]), .c_i(_18_c_i_1));
  fullAdder_main _18 (.c_i_1(_18_c_i_1), .s_i(r_18), .a_i(a_i[18]), .b_i(b_i[18]), .c_i(_17_c_i_1));
  fullAdder_main _17 (.c_i_1(_17_c_i_1), .s_i(r_17), .a_i(a_i[17]), .b_i(b_i[17]), .c_i(_16_c_i_1));
  fullAdder_main _16 (.c_i_1(_16_c_i_1), .s_i(r_16), .a_i(a_i[16]), .b_i(b_i[16]), .c_i(_15_c_i_1));
  fullAdder_main _15 (.c_i_1(_15_c_i_1), .s_i(r_15), .a_i(a_i[15]), .b_i(b_i[15]), .c_i(_14_c_i_1));
  fullAdder_main _14 (.c_i_1(_14_c_i_1), .s_i(r_14), .a_i(a_i[14]), .b_i(b_i[14]), .c_i(_13_c_i_1));
  fullAdder_main _12 (.c_i_1(_12_c_i_1), .s_i(r_12), .a_i(a_i[12]), .b_i(b_i[12]), .c_i(_11_c_i_1));
  fullAdder_main _13 (.c_i_1(_13_c_i_1), .s_i(r_13), .a_i(a_i[13]), .b_i(b_i[13]), .c_i(_12_c_i_1));
  fullAdder_main _11 (.c_i_1(_11_c_i_1), .s_i(r_11), .a_i(a_i[11]), .b_i(b_i[11]), .c_i(_10_c_i_1));
  fullAdder_main _10 (.c_i_1(_10_c_i_1), .s_i(r_10), .a_i(a_i[10]), .b_i(b_i[10]), .c_i(_9_c_i_1));
  fullAdder_main _8 (.c_i_1(_8_c_i_1), .s_i(r_8), .a_i(a_i[8]), .b_i(b_i[8]), .c_i(_7_c_i_1));
  fullAdder_main _9 (.c_i_1(_9_c_i_1), .s_i(r_9), .a_i(a_i[9]), .b_i(b_i[9]), .c_i(_8_c_i_1));
  fullAdder_main _7 (.c_i_1(_7_c_i_1), .s_i(r_7), .a_i(a_i[7]), .b_i(b_i[7]), .c_i(_6_c_i_1));
  fullAdder_main _6 (.c_i_1(_6_c_i_1), .s_i(r_6), .a_i(a_i[6]), .b_i(b_i[6]), .c_i(_5_c_i_1));
  fullAdder_main _4 (.c_i_1(_4_c_i_1), .s_i(r_4), .a_i(a_i[4]), .b_i(b_i[4]), .c_i(_3_c_i_1));
  fullAdder_main _5 (.c_i_1(_5_c_i_1), .s_i(r_5), .a_i(a_i[5]), .b_i(b_i[5]), .c_i(_4_c_i_1));
  fullAdder_main _3 (.c_i_1(_3_c_i_1), .s_i(r_3), .a_i(a_i[3]), .b_i(b_i[3]), .c_i(_2_c_i_1));
  fullAdder_main _2 (.c_i_1(_2_c_i_1), .s_i(r_2), .a_i(a_i[2]), .b_i(b_i[2]), .c_i(_1_c_i_1));
  fullAdder_main _1 (.c_i_1(_1_c_i_1), .s_i(r_1), .a_i(a_i[1]), .b_i(b_i[1]), .c_i(main_1_c_i_1));
  halfAdder_main main_1 (.c_i_1(main_1_c_i_1), .s_i(r_0), .a_i(a_i[0]), .b_i(b_i[0]));
endmodule
