// Logisim project 32Multiplier.circ as structural Verilog: 1 circuit, main circuit main
module main (
  input  [31:0] multiplier,
  input  [31:0] multiplicand,
  output [31:0] P_0,
  output [31:0] P_1,
  output carry_out
);

  wire clock_1_out, main_1_p0_e, main_1_p1_add, main_1_p1_e, main_1_p_s, main_2_p0_0, main_2_r_32, reset_out;

  Button reset (.out(reset_out));
  _32MultiplierControl_main main_1 (
    .reset(reset_out), .p0_0(main_2_p0_0), .s_32(main_2_r_32), .clk(clock_1_out), .P_S(main_1_p_s),
    .P1_add(main_1_p1_add), .P1_e(main_1_p1_e), .P0_e(main_1_p0_e));
  Clock clock_1 (.out(clock_1_out));
  _32MultiplierDatapath_main main_2 (
    .P_s(main_1_p_s), .P1_add(main_1_p1_add), .P1_e(main_1_p1_e), .P0_e(main_1_p0_e),
    .multiplier(multiplier), .multiplicand(multiplicand), .clk(clock_1_out), .P0_0(main_2_p0_0),
    .r_32(main_2_r_32), .P0(P_0), .P1(P_1), .c_out(carry_out));
endmodule
