// Logisim project 32MultiplierControl.circ as structural Verilog: 1 circuit, main circuit main
module main (
  input  p0_0,
  input  s_32,
  input  clk,
  input  reset,
  output P_S,
  output P1_add,
  output P1_e,
  output P0_e
);

  wire and_1_out, and_2_out, and_5_out, and_6_out, and_7_out, and_8_out, and_9_out, and_12_out, not_1_out,
       not_2_out, not_3_out, not_4_out, not_5_out, or_1_out, xnor_1_out, xor_1_out;
  wire [2:0] or_4_out, s_2_q;

  Register #(.width(3)) s_2 (.D(or_4_out), .Q(s_2_q), .clk(clk), .clr(reset));  // open: en
  not not_1 (not_1_out, p0_0);
  not not_2 (not_2_out, s_32);
  not not_3 (not_3_out, s_2_q[0]);
  not not_4 (not_4_out, s_2_q[1]);
  not not_5 (not_5_out, s_2_q[2]);
  and and_1 (and_1_out, not_4_out, not_1_out);
  and and_2 (and_2_out, s_2_q[1], not_2_out);
  and and_3 (P_S, not_5_out, s_2_q[1], s_2_q[0]);
  and and_4 (P1_add, not_5_out, s_2_q[1], not_3_out);
  and and_5 (and_5_out, not_5_out, not_3_out);
  and and_6 (and_6_out, not_5_out, s_2_q[1], s_2_q[0]);
  xnor xnor_1 (xnor_1_out, s_2_q[1], s_2_q[0]);
  and and_7 (and_7_out, s_32, s_2_q[0], s_2_q[1], not_5_out);
  and and_8 (and_8_out, s_2_q[2], not_4_out, not_3_out);
  xor xor_1 (xor_1_out, s_2_q[1], s_2_q[0]);
  and and_9 (and_9_out, not_5_out, not_3_out);
  or or_1 (or_1_out, and_1_out, and_2_out);
  or or_2 (P1_e, and_5_out, and_6_out);
  and and_10 (P0_e, not_5_out, xnor_1_out);
  and and_11 (or_4_out[1], not_5_out, xor_1_out);
  and and_12 (and_12_out, not_5_out, s_2_q[0], or_1_out);
  or or_3 (or_4_out[2], and_7_out, and_8_out);
  or or_4 (or_4_out[0], and_9_out, and_12_out);
endmodule
