// Logisim project 32MultiplierDatapath.circ as structural Verilog: 5 circuits, main circuit main
module main (
  input  [31:0] multiplicand,
  input  [31:0] multiplier,
  input  P_s,
  input  P1_add,
  input  P1_e,
  input  P0_e,
  input  clk,
  output P0_0,
  output r_32,
  output [31:0] P0,
  output [31:0] P1,
  output c_out
);

  wire [4:0] counter_1_q;
  wire [31:0] adder32_1_r_0, multiplexer_1_out, multiplexer_2_out, multiplexer_3_out, shifter64_1_out_0,
       shifter64_1_out_1;

  Counter #(.width(5), .max('h1f)) counter_1 (.count(P_s), .Q(counter_1_q), .clk(clk));  // open: load, D, carry, clr
  Comparator #(.width(5)) comparator_1 (.a(counter_1_q), .b({5{1'b1}}), .eq(r_32));  // open: gt, lt
  Multiplexer #(.width(32), .enable("false")) multiplexer_1 (
    .in0({32{1'b0}}), .in1(shifter64_1_out_1), .out(multiplexer_1_out), .sel(P_s));
  Multiplexer #(.width(32), .enable("false")) multiplexer_2 (
    .in0(multiplexer_1_out), .in1(adder32_1_r_0), .out(multiplexer_2_out), .sel(P1_add));
  Register #(.width(32)) product1 (.D(multiplexer_2_out), .en(P1_e), .Q(P1), .clk(clk));  // open: clr
  shifter64 shifter64_1 (.sh_r(P_s), .in_1(P1), .in_0(P0), .out_1(shifter64_1_out_1), .out_0(shifter64_1_out_0));
  Multiplexer #(.width(32), .enable("false")) multiplexer_3 (
    .in0(multiplier), .in1(shifter64_1_out_0), .out(multiplexer_3_out), .sel(P_s));
  Register #(.width(32)) product0 (.D(multiplexer_3_out), .en(P0_e), .Q(P0), .clk(clk));  // open: clr
  adder32 adder32_1 (
    .c_out(c_out), .a_i(P1), .b_i(multiplicand), .r_31(adder32_1_r_0[31]), .r_30(adder32_1_r_0[30]),
    .r_29(adder32_1_r_0[29]), .r_28(adder32_1_r_0[28]), .r_27(adder32_1_r_0[27]), .r_26(adder32_1_r_0[26]),
    .r_25(adder32_1_r_0[25]), .r_24(adder32_1_r_0[24]), .r_23(adder32_1_r_0[23]), .r_22(adder32_1_r_0[22]),
    .r_21(adder32_1_r_0[21]), .r_20(adder32_1_r_0[20]), .r_19(adder32_1_r_0[19]), .r_18(adder32_1_r_0[18]),
    .r_17(adder32_1_r_0[17]), .r_16(adder32_1_r_0[16]), .r_15(adder32_1_r_0[15]), .r_14(adder32_1_r_0[14]),
    .r_13(adder32_1_r_0[13]), .r_12(adder32_1_r_0[12]), .r_11(adder32_1_r_0[11]), .r_10(adder32_1_r_0[10]),
    .r_9(adder32_1_r_0[9]), .r_8(adder32_1_r_0[8]), .r_7(adder32_1_r_0[7]), .r_6(adder32_1_r_0[6]),
    .r_5(adder32_1_r_0[5]), .r_4(adder32_1_r_0[4]), .r_3(adder32_1_r_0[3]), .r_2(adder32_1_r_0[2]),
    .r_1(adder32_1_r_0[1]), .r_0(adder32_1_r_0[0]));

  assign P0_0 = P0[0];
endmodule

module halfAdder (
  input  a_i,
  input  b_i,
  output c_i_1,
  output s_i
);

  and and_1 (c_i_1, b_i, a_i);
  xor xor_1 (s_i, b_i, a_i);
endmodule

module fullAdder (
  input  a_i,
  input  b_i,
  input  c_i,
  output c_i_1,
  output s_i
);

  wire and_2_out, and_3_out, and_4_out, not_1_out, not_2_out, or_2_out, or_3_out;

  or or_1 (c_i_1, and_2_out, and_4_out);
  and and_1 (s_i, or_2_out, not_1_out);
  not not_1 (not_1_out, and_2_out);
  or or_2 (or_2_out, and_3_out, c_i);
  and and_2 (and_2_out, and_3_out, c_i);
  or or_3 (or_3_out, a_i, b_i);
  and and_3 (and_3_out, or_3_out, not_2_out);
  and and_4 (and_4_out, a_i, b_i);
  not not_2 (not_2_out, and_4_out);
endmodule

module adder32 (
  input  [31:0] a_i,
  input  [31:0] b_i,
  output c_out,
  output r_31,
  output r_30,
  output r_29,
  output r_28,
  output r_27,
  output r_26,
  output r_25,
  output r_24,
  output r_23,
  output r_22,
  output r_21,
  output r_20,
  output r_19,
  output r_18,
  output r_17,
  output r_16,
  output r_15,
  output r_14,
  output r_13,
  output r_12,
  output r_11,
  output r_10,
  output r_9,
  output r_8,
  output r_7,
  output r_6,
  output r_5,
  output r_4,
  output r_3,
  output r_2,
  output r_1,
  output r_0
);

  wire fulladder_2_c_i_1, fulladder_3_c_i_1, fulladder_4_c_i_1, fulladder_5_c_i_1, fulladder_6_c_i_1,
       fulladder_7_c_i_1, fulladder_8_c_i_1, fulladder_9_c_i_1, fulladder_10_c_i_1, fulladder_11_c_i_1,
       fulladder_12_c_i_1, fulladder_13_c_i_1, fulladder_14_c_i_1, fulladder_15_c_i_1, fulladder_16_c_i_1,
       fulladder_17_c_i_1, fulladder_18_c_i_1, fulladder_19_c_i_1, fulladder_20_c_i_1, fulladder_21_c_i_1,
       fulladder_22_c_i_1, fulladder_23_c_i_1, fulladder_24_c_i_1, fulladder_25_c_i_1, fulladder_26_c_i_1,
       fulladder_27_c_i_1, fulladder_28_c_i_1, fulladder_29_c_i_1, fulladder_30_c_i_1, fulladder_31_c_i_1,
       halfadder_1_c_i_1;

  fullAdder fulladder_1 (.c_i_1(c_out), .s_i(r_31), .a_i(a_i[31]), .b_i(b_i[31]), .c_i(fulladder_2_c_i_1));
  fullAdder fulladder_2 (.c_i_1(fulladder_2_c_i_1), .s_i(r_30), .a_i(a_i[30]), .b_i(b_i[30]), .c_i(fulladder_4_c_i_1));
  fullAdder fulladder_3 (.c_i_1(fulladder_3_c_i_1), .s_i(r_28), .a_i(a_i[28]), .b_i(b_i[28]), .c_i(fulladder_5_c_i_1));
  fullAdder fulladder_4 (.c_i_1(fulladder_4_c_i_1), .s_i(r_29), .a_i(a_i[29]), .b_i(b_i[29]), .c_i(fulladder_3_c_i_1));
  fullAdder fulladder_5 (.c_i_1(fulladder_5_c_i_1), .s_i(r_27), .a_i(a_i[27]), .b_i(b_i[27]), .c_i(fulladder_6_c_i_1));
  fullAdder fulladder_6 (.c_i_1(fulladder_6_c_i_1), .s_i(r_26), .a_i(a_i[26]), .b_i(b_i[26]), .c_i(fulladder_7_c_i_1));
  fullAdder fulladder_7 (.c_i_1(fulladder_7_c_i_1), .s_i(r_25), .a_i(a_i[25]), .b_i(b_i[25]), .c_i(fulladder_8_c_i_1));
  fullAdder fulladder_8 (.c_i_1(fulladder_8_c_i_1), .s_i(r_24), .a_i(a_i[24]), .b_i(b_i[24]), .c_i(fulladder_9_c_i_1));
  fullAdder fulladder_9 (.c_i_1(fulladder_9_c_i_1), .s_i(r_23), .a_i(a_i[23]), .b_i(b_i[23]), .c_i(fulladder_10_c_i_1));
  fullAdder fulladder_10 (
    .c_i_1(fulladder_10_c_i_1), .s_i(r_22), .a_i(a_i[22]), .b_i(b_i[22]), .c_i(fulladder_11_c_i_1));
  fullAdder fulladder_11 (
    .c_i_1(fulladder_11_c_i_1), .s_i(r_21), .a_i(a_i[21]), .b_i(b_i[21]), .c_i(fulladder_12_c_i_1));
  fullAdder fulladder_12 (
    .c_i_1(fulladder_12_c_i_1), .s_i(r_20), .a_i(a_i[20]), .b_i(b_i[20]), .c_i(fulladder_13_c_i_1));
  fullAdder fulladder_13 (
    .c_i_1(fulladder_13_c_i_1), .s_i(r_19), .a_i(a_i[19]), .b_i(b_i[19]), .c_i(fulladder_14_c_i_1));
  fullAdder fulladder_14 (
    .c_i_1(fulladder_14_c_i_1), .s_i(r_18), .a_i(a_i[18]), .b_i(b_i[18]), .c_i(fulladder_16_c_i_1));
  fullAdder fulladder_15 (
    .c_i_1(fulladder_15_c_i_1), .s_i(r_16), .a_i(a_i[16]), .b_i(b_i[16]), .c_i(fulladder_17_c_i_1));
  fullAdder fulladder_16 (
    .c_i_1(fulladder_16_c_i_1), .s_i(r_17), .a_i(a_i[17]), .b_i(b_i[17]), .c_i(fulladder_15_c_i_1));
  fullAdder fulladder_17 (
    .c_i_1(fulladder_17_c_i_1), .s_i(r_15), .a_i(a_i[15]), .b_i(b_i[15]), .c_i(fulladder_18_c_i_1));
  fullAdder fulladder_18 (
    .c_i_1(fulladder_18_c_i_1), .s_i(r_14), .a_i(a_i[14]), .b_i(b_i[14]), .c_i(fulladder_19_c_i_1));
  fullAdder fulladder_19 (
    .c_i_1(fulladder_19_c_i_1), .s_i(r_13), .a_i(a_i[13]), .b_i(b_i[13]), .c_i(fulladder_20_c_i_1));
  fullAdder fulladder_20 (
    .c_i_1(fulladder_20_c_i_1), .s_i(r_12), .a_i(a_i[12]), .b_i(b_i[12]), .c_i(fulladder_21_c_i_1));
  fullAdder fulladder_21 (
    .c_i_1(fulladder_21_c_i_1), .s_i(r_11), .a_i(a_i[11]), .b_i(b_i[11]), .c_i(fulladder_22_c_i_1));
  fullAdder fulladder_22 (
    .c_i_1(fulladder_22_c_i_1), .s_i(r_10), .a_i(a_i[10]), .b_i(b_i[10]), .c_i(fulladder_23_c_i_1));
  fullAdder fulladder_23 (.c_i_1(fulladder_23_c_i_1), .s_i(r_9), .a_i(a_i[9]), .b_i(b_i[9]), .c_i(fulladder_24_c_i_1));
  fullAdder fulladder_24 (.c_i_1(fulladder_24_c_i_1), .s_i(r_8), .a_i(a_i[8]), .b_i(b_i[8]), .c_i(fulladder_25_c_i_1));
  fullAdder fulladder_25 (.c_i_1(fulladder_25_c_i_1), .s_i(r_7), .a_i(a_i[7]), .b_i(b_i[7]), .c_i(fulladder_26_c_i_1));
  fullAdder fulladder_26 (.c_i_1(fulladder_26_c_i_1), .s_i(r_6), .a_i(a_i[6]), .b_i(b_i[6]), .c_i(fulladder_27_c_i_1));
  fullAdder fulladder_27 (.c_i_1(fulladder_27_c_i_1), .s_i(r_5), .a_i(a_i[5]), .b_i(b_i[5]), .c_i(fulladder_28_c_i_1));
  fullAdder fulladder_28 (.c_i_1(fulladder_28_c_i_1), .s_i(r_4), .a_i(a_i[4]), .b_i(b_i[4]), .c_i(fulladder_29_c_i_1));
  fullAdder fulladder_29 (.c_i_1(fulladder_29_c_i_1), .s_i(r_3), .a_i(a_i[3]), .b_i(b_i[3]), .c_i(fulladder_30_c_i_1));
  fullAdder fulladder_30 (.c_i_1(fulladder_30_c_i_1), .s_i(r_2), .a_i(a_i[2]), .b_i(b_i[2]), .c_i(fulladder_31_c_i_1));
  fullAdder fulladder_31 (.c_i_1(fulladder_31_c_i_1), .s_i(r_1), .a_i(a_i[1]), .b_i(b_i[1]), .c_i(halfadder_1_c_i_1));
  halfAdder halfadder_1 (.c_i_1(halfadder_1_c_i_1), .s_i(r_0), .a_i(a_i[0]), .b_i(b_i[0]));
endmodule

module shifter64 (
  input  [31:0] in_1,
  input  [31:0] in_0,
  input  sh_r,
  output [31:0] out_1,
  output [31:0] out_0
);

  Multiplexer #(.width(32)) multiplexer_1 (.in0(in_1), .in1({1'b0, in_1[31:1]}), .out(out_1), .sel(sh_r), .en(1'b1));
  Multiplexer #(.width(32)) multiplexer_2 (.in0(in_0), .in1({in_1[0], in_0[31:1]}), .out(out_0), .sel(sh_r), .en(1'b1));
endmodule
