// Logisim project 64Shifter.circ as structural Verilog: 1 circuit, main circuit main
module main (
  input  [31:0] in_1,
  input  [31:0] in_0,
  input  sh_r,
  output [31:0] out_1,
  output [31:0] out_0
);

  Multiplexer #(.width(32)) multiplexer_1 (.in0(in_1), .in1({1'b0, in_1[31:1]}), .out(out_1), .sel(sh_r), .en(1'b1));
  Multiplexer #(.width(32)) multiplexer_2 (.in0(in_0), .in1({in_1[0], in_0[31:1]}), .out(out_0), .sel(sh_r), .en(1'b1));
endmodule
