// Logisim project fullAdder.circ as structural Verilog: 1 circuit, main circuit main
module main (
  input  a_i,
  input  b_i,
  input  c_i,
  output c_i_1,
  output s_i
);

  wire and_2_out, and_3_out, and_4_out, not_1_out, not_2_out, or_2_out, or_3_out;

  or or_1 (c_i_1, and_2_out, and_4_out);
  and and_1 (s_i, or_2_out, not_1_out);
  not not_1 (not_1_out, and_2_out);
  or or_2 (or_2_out, and_3_out, c_i);
  and and_2 (and_2_out, and_3_out, c_i);
  or or_3 (or_3_out, a_i, b_i);
  and and_3 (and_3_out, or_3_out, not_2_out);
  not not_2 (not_2_out, and_4_out);
  and and_4 (and_4_out, a_i, b_i);
endmodule
