// Logisim project halfAdder.circ as structural Verilog: 1 circuit, main circuit main
module main (
  input  a_i,
  input  b_i,
  output c_i_1,
  output s_i
);

  and and_1 (c_i_1, b_i, a_i);
  xor xor_1 (s_i, b_i, a_i);
endmodule
